// Logisim project 161044116.circ as structural Verilog: 1 circuit, main circuit main
module main (
  input  [2:0] in_1,
  input  [2:0] in_2
);

  wire clock_1_out, decoder_1_out0, decoder_1_out1, decoder_1_out2, decoder_1_out3, decoder_1_out4,
       decoder_1_out5, decoder_1_out6, or_1_out;
  wire [2:0] adder_1_out, and_1_out, and_2_out, d_ff_1_q, or_2_out, subtractor_1_out;
  wire [2:2] button_1_out, button_2_out;

  Button button_1 (.out(button_1_out[2]));
  Button button_2 (.out(button_2_out[2]));
  Adder #(.width(3)) adder_1 (.a(d_ff_1_q), .b(in_1), .out(adder_1_out));  // open: cin, cout
  Subtractor #(.width(3)) subtractor_1 (.a(d_ff_1_q), .b(in_2), .out(subtractor_1_out));  // open: bin, bout
  assign and_1_out = adder_1_out & {3{button_1_out[2]}};  // AND_Gate and_1, 3 bits wide
  assign and_2_out = {3{button_2_out[2]}} & subtractor_1_out;  // AND_Gate and_2, 3 bits wide
  or or_1 (or_1_out, button_1_out[2], button_2_out[2]);
  assign or_2_out = and_1_out | and_2_out;  // OR_Gate or_2, 3 bits wide
  Clock clock_1 (.out(clock_1_out));
  D_Flip_Flop d_ff_1 (.clk(clock_1_out), .D(or_2_out[0]), .Q(d_ff_1_q[0]), .en(or_1_out));  // open: Qn, preset, reset
  D_Flip_Flop d_ff_2 (.clk(clock_1_out), .D(or_2_out[2]), .Q(d_ff_1_q[2]), .en(or_1_out));  // open: Qn, preset, reset
  D_Flip_Flop d_ff_3 (.clk(clock_1_out), .D(or_2_out[1]), .Q(d_ff_1_q[1]), .en(or_1_out));  // open: Qn, preset, reset
  Decoder #(.select(3)) decoder_1 (
    .out0(decoder_1_out0), .out1(decoder_1_out1), .out2(decoder_1_out2), .out3(decoder_1_out3),
    .out4(decoder_1_out4), .out5(decoder_1_out5), .out6(decoder_1_out6), .sel(d_ff_1_q));  // open: out7, en
  LED led_1 (.in(decoder_1_out0));
  LED led_2 (.in(decoder_1_out1));
  LED led_3 (.in(decoder_1_out2));
  LED led_4 (.in(decoder_1_out3));
  LED led_5 (.in(decoder_1_out4));
  LED led_6 (.in(decoder_1_out5));
  LED led_7 (.in(decoder_1_out6));
endmodule
