// Logisim project cntrl.circ as structural Verilog: 1 circuit, main circuit main
module main (
  input  Lt,
  input  gt,
  input  eq,
  input  go,
  input  clk,
  output Lb,
  output Sa,
  output La,
  output Lm,
  output [2:0] State
);

  wire and_1_out, and_2_out, and_3_out, and_4_out, and_5_out, and_6_out, and_7_out, and_8_out, not_1_out,
       not_3_out, s4_out, s5_out;
  wire [2:0] N1_out;

  Register #(.width(3)) u_State (.D(N1_out), .en(1'b1), .Q(State), .clk(clk));  // open: clr
  and and_1 (and_1_out, not_3_out, State[1], Lt, not_1_out);
  and and_2 (and_2_out, State[0], State[1], not_3_out);
  and and_3 (and_3_out, not_3_out, State[1], not_1_out, gt);
  and and_4 (and_4_out, eq, not_1_out, State[1], not_3_out);
  or N2 (N1_out[2], and_1_out, and_3_out, and_5_out, and_7_out);
  and and_5 (and_5_out, not_3_out, State[1], not_1_out, eq);
  and and_6 (and_6_out, Lt, not_1_out, State[1], not_3_out);
  or N1 (N1_out[0], and_2_out, and_4_out, and_6_out, and_8_out);
  and and_7 (and_7_out, not_3_out, State[1], State[0]);
  not not_1 (not_1_out, State[0]);
  not not_2 (N1_out[1], State[1]);
  not not_3 (not_3_out, State[2]);
  and and_8 (and_8_out, go, not_1_out, N1_out[1], not_3_out);
  and s1 (Lb, State[0], N1_out[1], not_3_out);
  and s4 (s4_out, N1_out[1], not_1_out, State[2]);
  and s5 (s5_out, State[0], N1_out[1], State[2]);
  or or_1 (La, Lb, s4_out);
  or or_2 (Lm, s4_out, s5_out);

  assign Sa = Lb;
endmodule
