// Logisim project datapath.circ as structural Verilog: 1 circuit, main circuit main
// b_i
module main (
  input  Lm,
  input  [15:0] b_i,
  input  Lb,
  input  [15:0] a_i,
  input  Sa,
  input  La,
  input  clk,
  output gt,
  output [15:0] mult,
  output eq,
  output lt
);

  wire adder_1_cout;
  wire [15:0] a_q, adder_1_out, b_q, bit_extender_1_out, multiplexer_1_out, subtractor_1_out;

  Multiplexer #(.width(16), .enable("false")) multiplexer_1 (
    .in0(subtractor_1_out), .in1(a_i), .out(multiplexer_1_out), .sel(Sa));
  Register #(.width(16)) u_mult (.D(adder_1_out), .en(Lm), .Q(mult), .clk(clk));  // open: clr
  Register #(.width(16)) b (.D(b_i), .en(Lb), .Q(b_q), .clk(clk));  // open: clr
  Register #(.width(16)) a (.D(multiplexer_1_out), .en(La), .Q(a_q), .clk(clk));  // open: clr
  Adder #(.width(16)) adder_1 (.a(b_q), .b(mult), .out(adder_1_out), .cin(1'b0), .cout(adder_1_cout));
  assign bit_extender_1_out = {{15{1'b0}}, 1'b1};  // Bit_Extender bit_extender_1
  Comparator #(.width(16)) comparator_1 (.a(a_q), .b({16{1'b0}}), .gt(gt), .eq(eq), .lt(lt));
  Subtractor #(.width(16)) subtractor_1 (
    .a(a_q), .b(bit_extender_1_out), .out(subtractor_1_out), .bin(1'b0));  // open: bout
endmodule
