// Logisim project main.circ as structural Verilog: 1 circuit, main circuit main
module main (
  input  [15:0] b_i,
  input  [15:0] a_i,
  input  go,
  output [15:0] mult,
  output [2:0] state
);

  wire clock_1_out, main_1_eq, main_1_gt, main_1_lt, main_2_la, main_2_lb, main_2_lm, main_2_sa;

  Clock clock_1 (.out(clock_1_out));
  datapath_main main_1 (
    .b_i(b_i), .Lb(main_2_lb), .a_i(a_i), .Sa(main_2_sa), .La(main_2_la), .clk(clock_1_out), .gt(main_1_gt),
    .Lm(main_2_lm), .lt(main_1_lt), .mult(mult), .eq(main_1_eq));
  cntrl_main main_2 (
    .Lt(main_1_lt), .gt(main_1_gt), .eq(main_1_eq), .go(go), .clk(clock_1_out), .State(state),
    .Lb(main_2_lb), .Sa(main_2_sa), .La(main_2_la), .Lm(main_2_lm));
endmodule
